# Fritzing sketch projeto_flitzing (saved by Fritzing 0.9.3b)
breadboards: 2

parts:
  R1 = Resistor [tolerance=±5% resistance=220 package=THT]
  C1 = Electrolytic Capacitor [capacitance=1µF package="100 mil [THT, electrolytic]"]
  S1 = H-Bridge with L298N
  U2 = POT [package=pot_alpha_rv16af-20]
  Mod2 = ESP32-TTGO-T-DISPLAY

nets:
  N1: R1.Pin_0, C1.+, Mod2.12
  N2: R1.Pin_1, U2.S
  N3: S1.ENA, Mod2.25
  N4: S1.IN1, Mod2.33
  N5: S1.IN2, Mod2.32
  N6: U2.A, Mod2.G-1, Mod2.G-2, Mod2.G-10, Mod2.G-11, Mod2.G-14
  N7: U2.E, Mod2.3V

custom parts:
  H-Bridge with L298N: h-bridge
  ESP32-TTGO-T-DISPLAY: LILYGO TTGO T-Display GD32VF103CBT6 Main Chip ST7789 1.14 Inch IPS 240x135 Resolution Minimalist Development Board.
